# Fritzing sketch netspresso_sketch (saved by Fritzing 1.0.0rc)

parts:
  Mod1 = Raspberry Pi Pico W
  Part1 = Adafruit ADS1115 16Bit I2C ADC [part_number="Adafruit #1085"]
  TRS1 = Audio Jack (TRS) 3.5mm [package="PG203J [THT]"]
  IC1 = DIP - 8 pins [chip_label=IC package="DIP (Dual Inline) [THT]"]

nets:
  N1: Mod1.pin_19, Part1.SDA
  N2: Mod1.pin_20, Part1.SCL
  N3: Mod1.pin_33, Mod1.pin_38, Part1.GND
  N4: Mod1.pin_36, Part1.VDD
  N5: Part1.AIN1, TRS1.Ring, IC1.Right
  N6: Part1.AIN0, TRS1.Sleeve, IC1.Ground
  N7: TRS1.Tip, IC1.Left

custom parts:
  Raspberry Pi Pico W: Raspberry Pi Pico W. Based around the RP2040 microcontroller the Pico W is a low cost microcontroller device bringing Raspberry Pi quality, cost, and easy of use to the microcontroller space. The areas marked KEEPOUT in pcb silkscreen should not have traces running through them to avoid shorts on a soldered in module!
  Adafruit ADS1115 16Bit I2C ADC: For microcontrollers without an analog-to-digital converter or when you want a higher-precision ADC, the ADS1115 provides 16-bit precision at 860 samples/second over I2C. The chip can be configured as 4 single-ended input channels, or two differential channels. As a nice bonus, it even includes a programmable gain amplifier, up to x16, to help boost up smaller single/differential signals to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
  DIP - 8 pins: A DIP stand-in part for whatever IC you want. With 8 pins on a 300mil dual inline package (DIP) footprint.
